// Logisim project Hack ALU.circ as structural Verilog: 1 circuit, main circuit main
module main (
  input  zx,
  input  nx,
  input  zy,
  input  ny,
  input  f,
  input  no,
  input  [15:0] x,
  input  [15:0] zeros,
  input  [15:0] y,
  output [15:0] out_10,
  output zr,
  output ng
);

  wire or_1_out;
  wire [15:0] adder_1_out, and_1_out, multiplexer_1_out, multiplexer_2_out, multiplexer_3_out,
       multiplexer_4_out, multiplexer_5_out, not_1_out, not_2_out, not_4_out;

  Multiplexer #(.width(16)) multiplexer_1 (.in0(x), .in1(zeros), .out(multiplexer_1_out), .sel(zx));  // open: en
  Multiplexer #(.width(16)) multiplexer_2 (.in0(y), .in1(zeros), .out(multiplexer_2_out), .sel(zy));  // open: en
  assign not_1_out = ~multiplexer_1_out;  // NOT_Gate not_1, 16 bits wide
  assign not_2_out = ~multiplexer_2_out;  // NOT_Gate not_2, 16 bits wide
  Multiplexer #(.width(16)) multiplexer_3 (
    .in0(multiplexer_1_out), .in1(not_1_out), .out(multiplexer_3_out), .sel(nx));  // open: en
  Multiplexer #(.width(16)) multiplexer_4 (
    .in0(multiplexer_2_out), .in1(not_2_out), .out(multiplexer_4_out), .sel(ny));  // open: en
  or or_1 (or_1_out, ng, out_10[14], out_10[13], out_10[12], out_10[11], out_10[10], out_10[9], out_10[8], out_10[7], out_10[6], out_10[5], out_10[4], out_10[3], out_10[2], out_10[1], out_10[0]);
  not not_3 (zr, or_1_out);
  assign and_1_out = multiplexer_3_out & multiplexer_4_out;  // AND_Gate and_1, 16 bits wide
  Adder #(.width(16)) adder_1 (.a(multiplexer_3_out), .b(multiplexer_4_out), .out(adder_1_out));  // open: cin, cout
  Multiplexer #(.width(16)) multiplexer_5 (
    .in0(and_1_out), .in1(adder_1_out), .out(multiplexer_5_out), .sel(f));  // open: en
  assign not_4_out = ~multiplexer_5_out;  // NOT_Gate not_4, 16 bits wide
  Multiplexer #(.width(16)) multiplexer_6 (
    .in0(multiplexer_5_out), .in1(not_4_out), .out({ng, out_10[14:0]}), .sel(no));  // open: en

  assign out_10[15] = ng;

  // Notes on the sheet:
  //   HACK ALU
  //   By
  //   Mahmoud Elshobaky
endmodule
